# Fritzing sketch v1 (saved by Fritzing 0.9.2b)
breadboards: 1

parts:
  J1 = T Cobbler Plus
  R1 = Resistor [tolerance=±5% resistance=1k package=THT]
  R2 = Resistor [tolerance=±5% resistance=1k package=THT]
  LED1 = LED - 5mm [color="Blue (470nm)" package="5 mm [THT]"]
  LED2 = LED - 5mm [color="Green (555nm)" package="5 mm [THT]"]
  U1 = mystery part, 8 pins [chip_label=MMA8451]
  U2 = mystery part, 6 pins [chip_label=TSL2591]

nets:
  N1: J1.5.0V#1, U1.pin7, U2.pin5
  N2: J1.SDA, U1.pin6, U2.pin6
  N3: J1.GND#8, U1.pin1
  N4: J1.#27, LED1.anode, LED2.anode, U1.pin2
  N5: J1.#24, R1.Pin_0
  N6: J1.MOSI, R2.Pin_0
  N7: J1.MISO, U2.pin1
  N8: J1.SCLK, U2.pin2
  N9: R1.Pin_1, LED2.cathode

custom parts:
  T Cobbler Plus: The T-Cobbler Plus is an add on prototyping board from Adafruit specifically designed for the Raspberry Pi B+ that can break out all those tasty power, GPIO, I2C and SPI pins from the 40-pin header onto a solderless breadboard. This set will make "cobbling together" prototypes with the Pi super easy. The T-Cobbler Plus can plug into any solderless breadboard.
